// Logisim project branch-comp.circ as structural Verilog: 1 circuit, main circuit branch_comp
module branch_comp (
  input  [31:0] rs1,
  input  [31:0] rs2,
  input  BrUn,
  output BrEq,
  output BrLt
);

  wire LT, UnLT;
  wire [32:32] undriven, undriven_2;

  Comparator #(.width(32)) comparator_1 (.a(rs1), .b(rs2), .eq(BrEq), .lt(LT));  // open: gt
  Comparator #(.mode("unsigned"), .width(33)) comparator_2 (
    .a({undriven[32], rs1}), .b({undriven_2[32], rs2}), .lt(UnLT));  // open: gt, eq
  Multiplexer #(.enable("false")) multiplexer_1 (.in0(LT), .in1(UnLT), .out(BrLt), .sel(BrUn));
  // Pins of 32 and 33 bits meet at {undriven[32], rs1}
  // Pins of 32 and 33 bits meet at {undriven_2[32], rs2}

  // Notes on the sheet:
  //   INPUTS to your circuit
  //   DON'T CHANGE THE LOCATIONS OF THE INPUTS AND OUTPUTS!
  //   OUTPUT from your circuit
endmodule
