// Logisim project control-logic.circ as structural Verilog: 5 circuits, main circuit control_logic
module control_logic (
  input  [31:0] inst,
  input  BrEq,
  input  BrLt,
  output PCSel,
  output RegWEn,
  output [2:0] ImmSel,
  output BrUn,
  output ASel,
  output BSel,
  output [3:0] ALUSel,
  output MemRW,
  output [1:0] WBSel,
  output CSRSel,
  output CSRWen,
  output [2:0] out_15,
  output [1:0] out_16
);

  wire multiplexer_2_out, multiplexer_6_out, multiplexer_8_out, multiplexer_11_out, multiplexer_12_out,
       multiplexer_13_out, not_1_out;
  wire [3:0] multiplexer_1_out, multiplexer_3_out, multiplexer_4_out, multiplexer_5_out, multiplexer_7_out,
       multiplexer_9_out, multiplexer_10_out;

  Multiplexer #(.enable("false"), .width(4)) multiplexer_1 (
    .in0(4'b0001), .in1(4'b1001), .out(multiplexer_1_out), .sel(inst[25]));
  Multiplexer #(.enable("false")) multiplexer_2 (.in0(BrEq), .in1(BrLt), .out(multiplexer_2_out), .sel(inst[14]));
  not not_1 (not_1_out, multiplexer_2_out);
  Multiplexer #(.enable("false"), .width(4)) multiplexer_3 (
    .in0(4'b0101), .in1(4'b1101), .out(multiplexer_3_out), .sel(inst[30]));
  Multiplexer #(.enable("false"), .select(2), .width(4)) multiplexer_4 (
    .in0(4'b0000), .in1(4'b1000), .in2(4'b1100), .out(multiplexer_4_out), .sel({inst[30], inst[25]}));  // open: in3
  Multiplexer #(.enable("false"), .width(4)) multiplexer_5 (
    .in0(4'b0101), .in1(4'b1101), .out(multiplexer_5_out), .sel(inst[30]));
  Multiplexer #(.enable("false")) multiplexer_6 (
    .in0(multiplexer_2_out), .in1(not_1_out), .out(multiplexer_6_out), .sel(inst[12]));
  Multiplexer #(.enable("false"), .select(3), .width(4)) multiplexer_7 (
    .in0(multiplexer_4_out), .in1(multiplexer_1_out), .in2(4'b0010), .in3(4'b1011), .in4(4'b0100),
    .in5(multiplexer_5_out), .in6(4'b0110), .in7(4'b0111), .out(multiplexer_7_out), .sel(inst[14:12]));
  opcode_select opcode_select_1 (
    .Load(1'b0), .I(1'b0), .S(1'b0), .R(1'b0), .U(1'b0), .SB(multiplexer_6_out), .jalr(1'b1), .J(1'b1),
    .CSR(1'b0), .in_10(inst[6:2]), .output_sel(PCSel));
  Multiplexer #(.enable("false")) multiplexer_8 (.in0(1'b0), .in1(1'b1), .out(multiplexer_8_out), .sel(inst[13]));
  Multiplexer #(.enable("false"), .select(3), .width(4)) multiplexer_9 (
    .in0(4'b0000), .in1(4'b0001), .in2(4'b0010), .in4(4'b0100), .in5(multiplexer_3_out), .in6(4'b0110),
    .in7(4'b0111), .out(multiplexer_9_out), .sel(inst[14:12]));  // open: in3
  Multiplexer #(.enable("false"), .width(4)) multiplexer_10 (
    .in0(4'b0000), .in1(4'b1111), .out(multiplexer_10_out), .sel(inst[5]));
  opcode_select opcode_select_2 (
    .Load(1'b0), .I(1'b0), .S(1'b0), .R(1'b0), .U(1'b0), .SB(multiplexer_8_out), .jalr(1'b0), .J(1'b0),
    .CSR(1'b0), .in_10(inst[6:2]), .output_sel(BrUn));
  Multiplexer #(.enable("false")) multiplexer_11 (.in0(1'b1), .in1(1'b0), .out(multiplexer_11_out), .sel(inst[5]));
  alu_select alu_select_1 (
    .Load(4'b0000), .I(multiplexer_9_out), .S(4'b0000), .R(multiplexer_7_out), .U(multiplexer_10_out),
    .SB(4'b0000), .jalr(4'b0000), .J(4'b0000), .CSR(multiplexer_9_out), .in_10(inst[6:2]),
    .output_alu_sel(ALUSel));
  opcode_select opcode_select_3 (
    .Load(1'b1), .I(1'b1), .S(1'b0), .R(1'b1), .U(1'b1), .SB(1'b0), .jalr(1'b1), .J(1'b1), .CSR(1'b0),
    .in_10(inst[6:2]), .output_sel(RegWEn));
  opcode_select opcode_select_4 (
    .Load(1'b0), .I(1'b0), .S(1'b0), .R(1'b0), .U(multiplexer_11_out), .SB(1'b1), .jalr(1'b0), .J(1'b1),
    .CSR(1'b0), .in_10(inst[6:2]), .output_sel(ASel));
  opcode_select opcode_select_5 (
    .Load(1'b0), .I(1'b0), .S(1'b1), .R(1'b0), .U(1'b0), .SB(1'b0), .jalr(1'b0), .J(1'b0), .CSR(1'b0),
    .in_10(inst[6:2]), .output_sel(MemRW));
  Multiplexer #(.enable("false"), .select(5)) multiplexer_12 (
    .in0(1'b0), .in1(1'b0), .in2(1'b0), .in3(1'b0), .in4(1'b0), .in5(1'b0), .in6(1'b0), .in7(1'b0),
    .in8(1'b0), .in9(1'b0), .in10(1'b0), .in11(1'b0), .in12(1'b0), .in13(1'b0), .in14(1'b0), .in15(1'b0),
    .in16(1'b0), .in17(1'b0), .in18(1'b0), .in19(1'b0), .in20(1'b0), .in21(1'b0), .in22(1'b0), .in23(1'b0),
    .in24(1'b0), .in25(1'b0), .in26(1'b0), .in27(1'b0), .in28(1'b1), .in29(1'b0), .in30(1'b0), .in31(1'b0),
    .out(multiplexer_12_out), .sel(inst[6:2]));
  Multiplexer #(.enable("false")) multiplexer_13 (.in0(1'b0), .in1(1'b1), .out(multiplexer_13_out), .sel(inst[14]));
  imm_select imm_select_1 (
    .Load(3'b000), .I(3'b000), .S(3'b001), .U(3'b011), .SB(3'b010), .jalr(3'b000), .J(3'b100), .CSR(3'b000),
    .in_10(inst[6:2]), .output_imm_sel(ImmSel));  // open: R
  opcode_select opcode_select_6 (
    .Load(1'b1), .I(1'b1), .S(1'b1), .R(1'b0), .U(1'b1), .SB(1'b1), .jalr(1'b1), .J(1'b1), .CSR(1'b1),
    .in_10(inst[6:2]), .output_sel(BSel));
  wb_select wb_select_1 (
    .Load(2'b10), .I(2'b01), .R(2'b01), .U(2'b01), .jalr(2'b00), .J(2'b00), .in_10(inst[6:2]),
    .output_wb_sel(WBSel));  // open: S, SB, CSR
  and and_1 (CSRSel, multiplexer_12_out, multiplexer_13_out);
  Multiplexer #(.enable("false"), .select(5)) multiplexer_14 (
    .in0(1'b0), .in1(1'b0), .in2(1'b0), .in3(1'b0), .in4(1'b0), .in5(1'b0), .in6(1'b0), .in7(1'b0),
    .in8(1'b0), .in9(1'b0), .in10(1'b0), .in11(1'b0), .in12(1'b0), .in13(1'b0), .in14(1'b0), .in15(1'b0),
    .in16(1'b0), .in17(1'b0), .in18(1'b0), .in19(1'b0), .in20(1'b0), .in21(1'b0), .in22(1'b0), .in23(1'b0),
    .in24(1'b0), .in25(1'b0), .in26(1'b0), .in27(1'b0), .in28(1'b1), .in29(1'b0), .in30(1'b0), .in31(1'b0),
    .out(CSRWen), .sel(inst[6:2]));

  assign out_15 = ImmSel;
  assign out_16 = {inst[30], inst[25]};

  // Other names for the same wires on the sheet: opcode[4:0] = inst[6:2]; funct3[2:0] = inst[14:12];
  //   funct7[6:0] = inst[31:25]; mul_sel[1:0] = {inst[30], inst[25]}

  // Notes on the sheet:
  //   INPUTS to your circuit
  //   DON'T CHANGE THE LOCATIONS OF THE INPUTS AND OUTPUTS!
  //   OUTPUT from your circuit
endmodule

module opcode_select (
  input  Load,
  input  I,
  input  S,
  input  R,
  input  U,
  input  SB,
  input  jalr,
  input  J,
  input  CSR,
  input  [4:0] in_10,
  output output_sel
);

  Multiplexer #(.enable("false"), .select(5)) multiplexer_1 (
    .in0(Load), .in4(I), .in5(U), .in8(S), .in12(R), .in13(U), .in24(SB), .in25(jalr), .in27(J), .in28(CSR),
    .out(output_sel), .sel(in_10));  // open: in1, in2, in3, in6, in7, in9, in10, in11, in14, in15, in16, in17, in18, in19, in20, in21, in22, in23, in26, in29, in30, in31
endmodule

module imm_select (
  input  [2:0] Load,
  input  [2:0] I,
  input  [2:0] S,
  input  [2:0] R,
  input  [2:0] U,
  input  [2:0] SB,
  input  [2:0] jalr,
  input  [2:0] J,
  input  [2:0] CSR,
  input  [4:0] in_10,
  output [2:0] output_imm_sel
);

  Multiplexer #(.enable("false"), .select(5), .width(3)) multiplexer_1 (
    .in0(Load), .in4(I), .in5(U), .in8(S), .in12(R), .in13(U), .in24(SB), .in25(jalr), .in27(J), .in28(CSR),
    .out(output_imm_sel), .sel(in_10));  // open: in1, in2, in3, in6, in7, in9, in10, in11, in14, in15, in16, in17, in18, in19, in20, in21, in22, in23, in26, in29, in30, in31
endmodule

module wb_select (
  input  [1:0] Load,
  input  [1:0] I,
  input  [1:0] S,
  input  [1:0] R,
  input  [1:0] U,
  input  [1:0] SB,
  input  [1:0] jalr,
  input  [1:0] J,
  input  [1:0] CSR,
  input  [4:0] in_10,
  output [1:0] output_wb_sel
);

  Multiplexer #(.enable("false"), .select(5), .width(2)) multiplexer_1 (
    .in0(Load), .in4(I), .in5(U), .in8(S), .in12(R), .in13(U), .in24(SB), .in25(jalr), .in27(J), .in28(CSR),
    .out(output_wb_sel), .sel(in_10));  // open: in1, in2, in3, in6, in7, in9, in10, in11, in14, in15, in16, in17, in18, in19, in20, in21, in22, in23, in26, in29, in30, in31
endmodule

module alu_select (
  input  [3:0] Load,
  input  [3:0] I,
  input  [3:0] S,
  input  [3:0] R,
  input  [3:0] U,
  input  [3:0] SB,
  input  [3:0] jalr,
  input  [3:0] J,
  input  [3:0] CSR,
  input  [4:0] in_10,
  output [3:0] output_alu_sel
);

  Multiplexer #(.enable("false"), .select(5), .width(4)) multiplexer_1 (
    .in0(Load), .in4(I), .in5(U), .in8(S), .in12(R), .in13(U), .in24(SB), .in25(jalr), .in27(J), .in29(CSR),
    .out(output_alu_sel), .sel(in_10));  // open: in1, in2, in3, in6, in7, in9, in10, in11, in14, in15, in16, in17, in18, in19, in20, in21, in22, in23, in26, in28, in30, in31
endmodule
