// Logisim project cpu.circ as structural Verilog: 1 circuit, main circuit cpu
module cpu (
  input  clk,
  input  [31:0] INSTRUCTION,
  input  [31:0] READ_DATA,
  output [31:0] WRITE_ADDRESS,
  output [31:0] PROGRAM_COUNTER,
  output [31:0] ra,
  output [31:0] sp,
  output [31:0] t0,
  output [31:0] t1,
  output [31:0] t2,
  output [31:0] s0,
  output [31:0] s1,
  output [31:0] a0,
  output [31:0] tohost,
  output [3:0] WRITE_ENABLE,
  output [31:0] WRITE_DATA
);

  wire ASel, BrEq, BrLt, BrUn, BSel, CSRSel, CSRWen, MemRW, PCSel, RegWEn;
  wire [1:0] WBSel;
  wire [2:0] ImmSel;
  wire [3:0] ALUSel, multiplexer_6_out, shifter_2_out;
  wire [4:0] bit_extender_2_out, multiplier_1_out;
  wire [7:0] multiplexer_7_out;
  wire [15:0] multiplexer_8_out;
  wire [31:0] adder_1_out, ALU_a, bit_extender_1_out, bit_extender_3_out, bit_extender_4_out, Imm_res,
       INSTRUCTION_pipeline, L_Data, multiplexer_1_out, multiplexer_2_out, multiplexer_3_out,
       multiplexer_5_out, PC_4, PROGRAM_COUNTER_pipeline, Read_Data_1, Read_Data_2, WB;

  Register #(.width(32)) PC (.D(multiplexer_1_out), .clk(clk), .Q(PROGRAM_COUNTER));  // open: en, clr
  Multiplexer #(.enable("false"), .width(32)) multiplexer_1 (
    .in0(adder_1_out), .in1(WRITE_ADDRESS), .out(multiplexer_1_out), .sel(PCSel));
  Register #(.width(32)) pc_pipe_reg (.D(PROGRAM_COUNTER), .clk(clk), .Q(PROGRAM_COUNTER_pipeline));  // open: en, clr
  Multiplexer #(.enable("false"), .width(32)) multiplexer_2 (
    .in0(INSTRUCTION), .in1(32'h13), .out(multiplexer_2_out), .sel(PCSel));
  Register #(.width(32)) inst_pipe_reg (.D(multiplexer_2_out), .clk(clk), .Q(INSTRUCTION_pipeline));  // open: en, clr
  Adder #(.width(32)) adder_1 (.a(PROGRAM_COUNTER), .b(32'h4), .out(adder_1_out));  // open: cin, cout
  regfile regfile_1 (
    .rs1(INSTRUCTION_pipeline[19:15]), .rs2(INSTRUCTION_pipeline[24:20]), .rd(INSTRUCTION_pipeline[11:7]),
    .Write_Data(WB), .RegWEn(RegWEn), .clk(clk), .ra(ra), .sp(sp), .t0(t0), .t1(t1), .t2(t2), .s0(s0),
    .s1(s1), .a0(a0), .Read_Data_1(Read_Data_1), .Read_Data_2(Read_Data_2));
  imm_gen imm_gen_1 (.inst(INSTRUCTION_pipeline), .ImmSel(ImmSel), .imm(Imm_res));
  Multiplexer #(.enable("false"), .width(32)) multiplexer_3 (
    .in0(Read_Data_1), .in1(bit_extender_1_out), .out(multiplexer_3_out), .sel(CSRSel));
  assign bit_extender_1_out = {{27{1'b0}}, INSTRUCTION_pipeline[19:15]};  // Bit_Extender bit_extender_1
  control_logic control_logic_1 (
    .inst(INSTRUCTION_pipeline), .BrEq(BrEq), .BrLt(BrLt), .PCSel(PCSel), .RegWEn(RegWEn), .ImmSel(ImmSel),
    .BrUn(BrUn), .ASel(ASel), .BSel(BSel), .ALUSel(ALUSel), .MemRW(MemRW), .WBSel(WBSel), .CSRSel(CSRSel),
    .CSRWen(CSRWen));  // open: out_15, out_16
  branch_comp branch_comp_1 (.rs1(Read_Data_1), .rs2(Read_Data_2), .BrUn(BrUn), .BrEq(BrEq), .BrLt(BrLt));
  Multiplexer #(.enable("false"), .width(32)) multiplexer_4 (
    .in0(Read_Data_1), .in1(PROGRAM_COUNTER_pipeline), .out(ALU_a), .sel(ASel));
  // csr csr_1: pin names not known; wires that end beside it: INSTRUCTION_pipeline[31:20], multiplexer_3_out, CSRWen, clk, tohost
  Multiplexer #(.enable("false"), .width(32)) multiplexer_5 (
    .in0(Read_Data_2), .in1(Imm_res), .out(multiplexer_5_out), .sel(BSel));
  alu alu_1 (.Result(WRITE_ADDRESS), .A(ALU_a), .B(multiplexer_5_out), .ALUSel(ALUSel));
  assign bit_extender_2_out = {{3{WRITE_ADDRESS[1]}}, WRITE_ADDRESS[1:0]};  // Bit_Extender bit_extender_2
  Multiplexer #(.enable("false"), .select(2), .width(4)) multiplexer_6 (
    .in0(4'b0001), .in1(4'b0011), .in2(4'b1111), .out(multiplexer_6_out), .sel(INSTRUCTION_pipeline[13:12]));  // open: in3
  Multiplier #(.width(5)) multiplier_1 (
    .a(bit_extender_2_out), .b(5'b01000), .out(multiplier_1_out));  // open: cin, cout
  Adder #(.width(32)) adder_2 (.a(PROGRAM_COUNTER_pipeline), .b(32'h4), .out(PC_4));  // open: cin, cout
  Shifter #(.width(32)) shifter_1 (.in(Read_Data_2), .\dist (multiplier_1_out), .out(WRITE_DATA));
  Shifter #(.width(4)) shifter_2 (.in(multiplexer_6_out), .\dist (WRITE_ADDRESS[1:0]), .out(shifter_2_out));
  Multiplexer #(.enable("false"), .select(2), .width(8)) multiplexer_7 (
    .in0(READ_DATA[7:0]), .in1(READ_DATA[15:8]), .in2(READ_DATA[23:16]), .in3(READ_DATA[31:24]),
    .out(multiplexer_7_out), .sel(WRITE_ADDRESS[1:0]));
  Multiplexer #(.enable("false"), .width(16)) multiplexer_8 (
    .in0(READ_DATA[15:0]), .in1(READ_DATA[31:16]), .out(multiplexer_8_out), .sel(WRITE_ADDRESS[1]));
  Multiplexer #(.enable("false"), .width(4)) multiplexer_9 (
    .in0(4'b0000), .in1(shifter_2_out), .out(WRITE_ENABLE), .sel(MemRW));
  assign bit_extender_3_out = {{24{multiplexer_7_out[7]}}, multiplexer_7_out};  // Bit_Extender bit_extender_3
  assign bit_extender_4_out = {{16{multiplexer_8_out[15]}}, multiplexer_8_out};  // Bit_Extender bit_extender_4
  Multiplexer #(.enable("false"), .select(2), .width(32)) multiplexer_10 (
    .in0(bit_extender_3_out), .in1(bit_extender_4_out), .in2(READ_DATA), .out(L_Data),
    .sel(INSTRUCTION_pipeline[13:12]));  // open: in3
  Multiplexer #(.enable("false"), .select(2), .width(32)) multiplexer_11 (
    .in0(PC_4), .in1(WRITE_ADDRESS), .in2(L_Data), .out(WB), .sel(WBSel));  // open: in3

  // Other names for the same wires on the sheet: ALU_out[31:0] = WRITE_ADDRESS

  // Notes on the sheet:
  //   Output to IMEM
  //   IMEM (do **NOT** move this)
  //   Inputs from IMEM
  //   It is OK to move the PC, RegFile, ALU, MEM, Branch Comp, Imm Gen, and Control Logic to wherever is most convenient for you when constructing your CPU, and to delete this text
  //   Inputs/Outputs for testing. Do **NOT** move these.
  //   Outputs To DMEM
  //   DMEM (do **NOT** move this)
  //   Inputs From DMEM
endmodule
