// Logisim project regfile.circ as structural Verilog: 1 circuit, main circuit regfile
module regfile (
  input  [4:0] rs1,
  input  [4:0] rs2,
  input  [4:0] rd,
  input  [31:0] Write_Data,
  input  RegWEn,
  input  clk,
  output [31:0] ra,
  output [31:0] sp,
  output [31:0] t0,
  output [31:0] t1,
  output [31:0] t2,
  output [31:0] s0,
  output [31:0] s1,
  output [31:0] a0,
  output [31:0] Read_Data_1,
  output [31:0] Read_Data_2
);

  wire i1, i2, i3, i4, i5, i6, i7, i8, i9, i10, i11, i12, i13, i14, i15, i16, i17, i18, i19, i20, i21, i22,
       i23, i24, i25, i26, i27, i28, i29, i30, i31, i32;
  wire [31:0] a1, a2, a3, a4, a5, a6, a7, gp, s2, s3, s4, s5, s6, s7, s8, s9, s10, s11, t3, t4, t5, t6, tp,
       x0;

  Demultiplexer #(.enable("false"), .select(5)) demultiplexer_1 (
    .out0(i1), .out1(i2), .out2(i3), .out3(i4), .out4(i5), .out5(i6), .out6(i7), .out7(i8), .out8(i9),
    .out9(i10), .out10(i11), .out11(i12), .out12(i13), .out13(i14), .out14(i15), .out15(i16), .out16(i17),
    .out17(i18), .out18(i19), .out19(i20), .out20(i21), .out21(i22), .out22(i23), .out23(i24), .out24(i25),
    .out25(i26), .out26(i27), .out27(i28), .out28(i29), .out29(i30), .out30(i31), .out31(i32), .in(RegWEn),
    .sel(rd));
  Register #(.width(32)) register_1 (.D({32{1'b0}}), .clk(clk), .Q(x0));  // open: en, clr
  Register #(.width(32)) reg1 (.D(Write_Data), .en(i2), .clk(clk), .Q(ra));  // open: clr
  Register #(.width(32)) reg2 (.D(Write_Data), .en(i3), .clk(clk), .Q(sp));  // open: clr
  Register #(.width(32)) reg3 (.D(Write_Data), .en(i4), .clk(clk), .Q(gp));  // open: clr
  Register #(.width(32)) reg4 (.D(Write_Data), .en(i5), .clk(clk), .Q(tp));  // open: clr
  Register #(.width(32)) reg5 (.D(Write_Data), .en(i6), .clk(clk), .Q(t0));  // open: clr
  Register #(.width(32)) reg6 (.D(Write_Data), .en(i7), .clk(clk), .Q(t1));  // open: clr
  Register #(.width(32)) reg7 (.D(Write_Data), .en(i8), .clk(clk), .Q(t2));  // open: clr
  Register #(.width(32)) reg8 (.D(Write_Data), .en(i9), .clk(clk), .Q(s0));  // open: clr
  Register #(.width(32)) reg9 (.D(Write_Data), .en(i10), .clk(clk), .Q(s1));  // open: clr
  Register #(.width(32)) reg10 (.D(Write_Data), .en(i11), .clk(clk), .Q(a0));  // open: clr
  Register #(.width(32)) reg11 (.D(Write_Data), .en(i12), .clk(clk), .Q(a1));  // open: clr
  Register #(.width(32)) register_2 (.D(Write_Data), .en(i13), .clk(clk), .Q(a2));  // open: clr
  Register #(.width(32)) register_3 (.D(Write_Data), .en(i14), .clk(clk), .Q(a3));  // open: clr
  Register #(.width(32)) register_4 (.D(Write_Data), .en(i15), .clk(clk), .Q(a4));  // open: clr
  Register #(.width(32)) register_5 (.D(Write_Data), .en(i16), .clk(clk), .Q(a5));  // open: clr
  Register #(.width(32)) register_6 (.D(Write_Data), .en(i17), .clk(clk), .Q(a6));  // open: clr
  Register #(.width(32)) register_7 (.D(Write_Data), .en(i18), .clk(clk), .Q(a7));  // open: clr
  Register #(.width(32)) register_8 (.D(Write_Data), .en(i19), .clk(clk), .Q(s2));  // open: clr
  Register #(.width(32)) register_9 (.D(Write_Data), .en(i20), .clk(clk), .Q(s3));  // open: clr
  Register #(.width(32)) register_10 (.D(Write_Data), .en(i21), .clk(clk), .Q(s4));  // open: clr
  Multiplexer #(.enable("false"), .select(5), .width(32)) multiplexer_1 (
    .in0(x0), .in1(ra), .in2(sp), .in3(gp), .in4(tp), .in5(t0), .in6(t1), .in7(t2), .in8(s0), .in9(s1),
    .in10(a0), .in11(a1), .in12(a2), .in13(a3), .in14(a4), .in15(a5), .in16(a6), .in17(a7), .in18(s2),
    .in19(s3), .in20(s4), .in21(s5), .in22(s6), .in23(s7), .in24(s8), .in25(s9), .in26(s10), .in27(s11),
    .in28(t3), .in29(t4), .in30(t5), .in31(t6), .out(Read_Data_1), .sel(rs1));
  Register #(.width(32)) register_11 (.D(Write_Data), .en(i22), .clk(clk), .Q(s5));  // open: clr
  Register #(.width(32)) register_12 (.D(Write_Data), .en(i23), .clk(clk), .Q(s6));  // open: clr
  Register #(.width(32)) register_13 (.D(Write_Data), .en(i24), .clk(clk), .Q(s7));  // open: clr
  Register #(.width(32)) register_14 (.D(Write_Data), .en(i25), .clk(clk), .Q(s8));  // open: clr
  Register #(.width(32)) register_15 (.D(Write_Data), .en(i26), .clk(clk), .Q(s9));  // open: clr
  Register #(.width(32)) register_16 (.D(Write_Data), .en(i27), .clk(clk), .Q(s10));  // open: clr
  Register #(.width(32)) register_17 (.D(Write_Data), .en(i28), .clk(clk), .Q(s11));  // open: clr
  Register #(.width(32)) register_18 (.D(Write_Data), .en(i29), .clk(clk), .Q(t3));  // open: clr
  Multiplexer #(.enable("false"), .select(5), .width(32)) multiplexer_2 (
    .in0(x0), .in1(ra), .in2(sp), .in3(gp), .in4(tp), .in5(t0), .in6(t1), .in7(t2), .in8(s0), .in9(s1),
    .in10(a0), .in11(a1), .in12(a2), .in13(a3), .in14(a4), .in15(a5), .in16(a6), .in17(a7), .in18(s2),
    .in19(s3), .in20(s4), .in21(s5), .in22(s6), .in23(s7), .in24(s8), .in25(s9), .in26(s10), .in27(s11),
    .in28(t3), .in29(t4), .in30(t5), .in31(t6), .out(Read_Data_2), .sel(rs2));
  Register #(.width(32)) register_19 (.D(Write_Data), .en(i30), .clk(clk), .Q(t4));  // open: clr
  Register #(.width(32)) register_20 (.D(Write_Data), .en(i31), .clk(clk), .Q(t5));  // open: clr
  Register #(.width(32)) register_21 (.D(Write_Data), .en(i32), .clk(clk), .Q(t6));  // open: clr

  // Other names for the same wires on the sheet: read_data1[31:0] = Read_Data_1; read_data2[31:0] = Read_Data_2;
  //   read_reg1[4:0] = rs1; read_reg2[4:0] = rs2; write_en = RegWEn; write_reg[4:0] = rd

  // Notes on the sheet:
  //   INPUTS to your circuit
  //   DON'T CHANGE THE LOCATIONS OF THE INPUTS AND OUTPUTS!
  //   These are DEBUG/TEST outputs from your circuit.
  //   OUTPUTS from your circuit
endmodule
