// Logisim project cpu-test_i.circ as structural Verilog: 1 circuit, main circuit run_main
module run_main (
  output [31:0] ra,
  output [31:0] sp,
  output [31:0] t0,
  output [31:0] t1,
  output [31:0] t2,
  output [31:0] s0,
  output [31:0] s1,
  output [31:0] a0,
  output [31:0] Requested_Address,
  output [31:0] Requested_Instruction,
  output [15:0] Time_Step,
  output halt
);

  wire clk;

  Clock clock_1 (.out(clk));
  // Probe on Requested_Address
  // cpu_harness cpu_harness_1: pin names not known; wires that end beside it: Requested_Instruction, clk, Requested_Address, ra, sp, t0, t1, t2, s0, s1, a0
  ROM #(.addrWidth(14), .dataWidth(32)) rom_1 (.addr(Requested_Address[15:2]), .data(Requested_Instruction));
  // Probe on Requested_Instruction
  Counter #(.max('hffff), .width(16)) counter_1 (.clk(clk), .Q(Time_Step));  // open: clr, load, up, count, D, carry
  Comparator #(.width(16)) comparator_1 (.a(Time_Step), .b(16'h38), .eq(halt));  // open: gt, lt

  // Other names for the same wires on the sheet: INSTRUCTION[31:0] = Requested_Instruction;
  //   PROGRAM_COUNTER[31:0] = Requested_Address

  // Notes on the sheet:
  //   contents of rom_1 (hex, n*v repeats v):
  //   6F00013 FCE08093 409113 1F09193 4570C213 FFB0C293 40D313 1F0D393 4040D413 41F0D493 4040D513 41F0D593
  //   40E513 FFC0E593 40F593 FFC0F613 13 6F08093 FCE10113 6F18193 FCE20213 6F28293 FCE30313 6F38393
  //   FCE40413 6F48493 FCE50513 6F58593 FCE60613 6F68693 FCE70713 6F78793 FCE80813 6F88893 FCE90913
  //   6F98993 FCEA0A13 6FA8A93 FCEB0B13 6FB8B93 FCEC0C13 6FC8C93 FCED0D13 FCED8D93 6FE0E13 FCEE8E93
  //   6FF0F13 FCEF8F93 100117 100117 80000413 FFFFF437 DEADA537 EEF50513
  //   Instruction Memory
  //   Halts Execution After Constant # of Clock Cycles
  //   Constant
endmodule
