// Logisim project cpu-test_mem.circ as structural Verilog: 1 circuit, main circuit run_main
module run_main (
  output [31:0] ra,
  output [31:0] sp,
  output [31:0] t0,
  output [31:0] t1,
  output [31:0] t2,
  output [31:0] s0,
  output [31:0] s1,
  output [31:0] a0,
  output [31:0] Requested_Address,
  output [31:0] Requested_Instruction,
  output [15:0] Time_Step,
  output halt
);

  wire clk;

  Clock clock_1 (.out(clk));
  // Probe on Requested_Address
  // cpu_harness cpu_harness_1: pin names not known; wires that end beside it: Requested_Instruction, clk, Requested_Address, ra, sp, t0, t1, t2, s0, s1, a0
  ROM #(.addrWidth(14), .dataWidth(32)) rom_1 (.addr(Requested_Address[15:2]), .data(Requested_Instruction));
  // Probe on Requested_Instruction
  Counter #(.max('hffff), .width(16)) counter_1 (.clk(clk), .Q(Time_Step));  // open: clr, load, up, count, D, carry
  Comparator #(.width(16)) comparator_1 (.a(Time_Step), .b(16'h3e), .eq(halt));  // open: gt, lt

  // Other names for the same wires on the sheet: INSTRUCTION[31:0] = Requested_Instruction;
  //   PROGRAM_COUNTER[31:0] = Requested_Address

  // Notes on the sheet:
  //   contents of rom_1 (hex, n*v repeats v):
  //   AB00093 19000113 21106A3 2110723 21107A3 2110823 2D10083 2E10083 2F10083 3010083 111023 1110A3
  //   111123 11083 111083 211083 6111C23 6111CA3 6111D23 7811083 7911083 7A11083 112023 112223 112423
  //   12083 412083 812083 80000093 19000113 FE110FA3 FE110F23 FE110CA3 FFF10083 FFE10083 FF910083 FE111FA3
  //   FE111F23 FE111DA3 FFF10083 FFE10083 FFB10083 FE112E23 FFC12083 80000093 F9C00113 1105A3 B10083
  //   1112A3 511083 112023 12083 80000093 7FF00113 1105A3 B10083 1112A3 511083 112023 12083
  //   Instruction Memory
  //   Halts Execution After Constant # of Clock Cycles
  //   Constant
endmodule
